# Fritzing sketch duo (saved by Fritzing 0.9.3b)
breadboards: 1

parts:
  Part1 = Arduino Uno (Rev3)
  LED1 = DUO LED RG [package="5 mm [THT]"]
  S1 = Pushbutton [package="[THT]"]
  S2 = Pushbutton [package="[THT]"]

nets:
  N1: Part1.3V3, S1.Pin_1, S1.Pin_2, S2.Pin_1, S2.Pin_2
  N2: Part1.GND, LED1.common_cathode
  N3: LED1.red_anode, S1.Pin_3, S1.Pin_4
  N4: LED1.green_anode, S2.Pin_3, S2.Pin_4
